# Fritzing sketch refsignal_nodeteensy_setup (saved by Fritzing 0.9.3b)
breadboards: 1

parts:
  U1 = NodeMCU V1.0
  Teensy_3_1 = Teensy 3.1
  U2 = LM124-324 Quad Opamp [package="DIP (Dual Inline)"]
  R1 = Resistor [tolerance=±1% resistance=100k package="0402 [SMD]"]
  R2 = Resistor [tolerance=±5% resistance=39k package="0402 [SMD]"]
  C1 = Electrolytic Capacitor [capacitance=1000μF package="1010 [SMD, electrolytic]"]

nets:
  N1: U1.GND, U2.VCC-, C1.-
  N2: U1.Vin, C1.+
  N3: Teensy_3_1.A14/DAC, U2.4IN+
  N4: U2.VCC+, R1.Pin_1
  N5: U2.4IN-, R2.Pin_0
  N6: U2.4OUT, R2.Pin_1

custom parts:
  NodeMCU V1.0: ESP8266 based NodeMCU
